// Logisim project Skhema_Lab1.circ as structural Verilog: 1 circuit, main circuit main
module main (
  input  \А1 ,
  input  \А0 ,
  input  \В1 ,
  input  \В0 ,
  input  \Р ,
  output out_6,
  output S1,
  output S0
);

  wire and_1_out, and_2_out, and_3_out, and_4_out, and_5_out, and_6_out, and_7_out, and_8_out, and_9_out,
       and_10_out, and_11_out, and_12_out, and_13_out, and_14_out, and_15_out, and_16_out, and_17_out,
       not_1_out, not_2_out, not_3_out, not_4_out, not_5_out, or_1_out, xor_1_out, xor_2_out, xor_3_out;

  not not_1 (not_1_out, \А1 );
  not not_2 (not_2_out, \А0 );
  not not_3 (not_3_out, \В1 );
  not not_4 (not_4_out, \В0 );
  not not_5 (not_5_out, \Р );
  and and_1 (and_1_out, \А1 , not_2_out, not_3_out, not_4_out);
  and and_2 (and_2_out, \А1 , not_2_out, not_3_out, not_5_out);
  and and_3 (and_3_out, \А0 , \А1 , \В0 , \В1 );
  and and_4 (and_4_out, \А1 , \А0 , \В1 , \Р );
  and and_5 (and_5_out, \А1 , \В1 , \В0 , \Р );
  and and_6 (and_6_out, \А1 , not_3_out, not_4_out, not_5_out);
  xor xor_1 (xor_1_out, \А0 , \В0 );
  xor xor_2 (xor_2_out, \А1 , \В1 );
  and and_7 (and_7_out, not_1_out, \А0 , not_3_out, \В0 );
  and and_8 (and_8_out, not_1_out, \А0 , not_3_out, \Р );
  and and_9 (and_9_out, \А1 , \В1 );
  xor xor_3 (xor_3_out, \А0 , \В0 );
  xor xor_4 (S0, xor_1_out, \Р );
  and and_10 (and_10_out, xor_3_out, \Р );
  and and_11 (and_11_out, not_1_out, not_2_out, \В1 );
  and and_12 (and_12_out, \А0 , \В0 );
  and and_13 (and_13_out, and_11_out, not_4_out);
  and and_14 (and_14_out, and_11_out, not_5_out);
  and and_15 (and_15_out, not_1_out, \В1 , not_4_out, not_5_out);
  and and_16 (and_16_out, not_1_out, not_3_out, \В0 , \Р );
  or or_1 (or_1_out, and_12_out, and_10_out);
  and and_17 (and_17_out, xor_2_out, or_1_out);
  or or_2 (S1, and_13_out, and_14_out, and_7_out, and_1_out, and_2_out, and_3_out, and_15_out, and_4_out, and_8_out, and_5_out, and_16_out, and_6_out);
  or or_3 (out_6, and_9_out, and_17_out);

  // Notes on the sheet:
  //   S2
endmodule
