// Logisim project ла.circ as structural Verilog: 1 circuit, main circuit main
module main (
);

  wire and_1_out, and_2_out, and_3_out, and_4_out, and_5_out, and_6_out, and_7_out, and_8_out, and_9_out,
       and_10_out, and_11_out, and_12_out, and_13_out, not_1_out, or_1_out, undriven, undriven_2, undriven_3,
       undriven_4, undriven_5, undriven_6, undriven_7, undriven_8, undriven_9, undriven_10, undriven_11,
       undriven_12, undriven_13, undriven_14, undriven_15, undriven_16, undriven_17, undriven_18,
       undriven_19, undriven_20, undriven_21, undriven_22, undriven_23, undriven_24, undriven_25,
       undriven_26, undriven_27, undriven_28, undriven_29, undriven_30, undriven_31, undriven_32, undriven_33;

  // NOT_Gate not_1 has open pins: in=open, out=not_1_out
  and and_1 (and_1_out, undriven, undriven_2, undriven_3, undriven_4);
  and and_2 (and_2_out, undriven_15, undriven_16, undriven_17, undriven_18);
  and and_3 (and_3_out, undriven_9, undriven_6, undriven_7, undriven_5);
  and and_4 (and_4_out, undriven_8, undriven_10, undriven_11, undriven_12);
  and and_5 (and_5_out, not_1_out, undriven_22, undriven_23, undriven_24, undriven_25);
  and and_6 (and_6_out, not_1_out, undriven_26, undriven_27, undriven_28);
  and and_7 (and_7_out, undriven_30, undriven_14, undriven_19);
  and and_8 (and_8_out, undriven_20, undriven_21, undriven_13, undriven_31);
  and and_9 (and_9_out, not_1_out, undriven_29, undriven_30);
  and and_10 (and_10_out, and_9_out, undriven_13);
  and and_11 (and_11_out, and_9_out, undriven_31);
  and and_12 (and_12_out, undriven_32, undriven_30, undriven_13, undriven_31);
  and and_13 (and_13_out, not_1_out, undriven_27, undriven_14, undriven_33);
  or or_1 (or_1_out, and_10_out, and_11_out, and_5_out, and_1_out, and_2_out, and_3_out, and_12_out, and_4_out, and_6_out, and_7_out, and_13_out, and_8_out);
endmodule
