// Logisim project лаба1.circ as structural Verilog: 1 circuit, main circuit main
module main (
  input  \А1 ,
  input  \В1 ,
  input  Bo,
  input  \Ао ,
  input  p,
  input  in_6,
  input  \р ,
  input  p_2,
  input  B1,
  input  A1,
  input  Ao,
  input  Bo_2,
  output S2,
  output So,
  output So_2,
  output out_16,
  output S2_2
);

  wire and_1_out, and_2_out, and_3_out, and_4_out, and_5_out, and_6_out, and_7_out, and_8_out, and_9_out,
       and_10_out, and_11_out, and_12_out, and_13_out, and_14_out, and_15_out, and_16_out, or_1_out,
       or_2_out, or_3_out, xor_3_out, xor_4_out, xor_5_out, xor_6_out, xor_7_out, xor_8_out, xor_9_out,
       xor_10_out, xor_11_out, xor_12_out, xor_13_out, xor_15_out;

  xor xor_1 (So, Bo, p);
  xor xor_2 (So_2, Bo_2, p_2);
  or or_1 (or_1_out, p_2, B1);
  and and_1 (and_1_out, p_2, B1);
  and and_2 (and_2_out, Ao, Bo_2);
  xor xor_3 (xor_3_out, or_1_out, A1);
  and and_3 (and_3_out, and_1_out, Bo_2);
  and and_4 (and_4_out, and_2_out, p_2);
  and and_5 (and_5_out, A1, B1);
  xor xor_4 (xor_4_out, A1, B1);
  or or_2 (or_2_out, xor_3_out, and_1_out);
  and and_6 (and_6_out, Ao, Bo_2);
  and and_7 (and_7_out, B1, p_2, Ao);
  xor xor_5 (xor_5_out, Ao, Bo_2);
  xor xor_6 (xor_6_out, or_2_out, and_2_out);
  and and_8 (and_8_out, xor_5_out, p_2);
  xor xor_7 (xor_7_out, xor_6_out, and_3_out);
  and and_9 (and_9_out, and_4_out, B1);
  xor xor_8 (xor_8_out, and_8_out, and_6_out);
  xor xor_9 (xor_9_out, \А1 , \В1 );
  xor xor_10 (xor_10_out, \Ао , in_6);
  xor xor_11 (xor_11_out, xor_7_out, and_4_out);
  and and_10 (and_10_out, and_7_out, A1);
  and and_11 (and_11_out, xor_4_out, xor_8_out);
  and and_12 (and_12_out, \А1 , \В1 );
  and and_13 (and_13_out, xor_10_out, \р );
  and and_14 (and_14_out, \Ао , in_6);
  xor xor_12 (xor_12_out, xor_11_out, and_7_out);
  xor xor_13 (xor_13_out, xor_12_out, and_9_out);
  xor xor_14 (S2_2, and_5_out, and_11_out);
  or or_3 (or_3_out, and_13_out, and_14_out);
  xor xor_15 (xor_15_out, xor_13_out, and_10_out);
  and and_15 (and_15_out, and_10_out, Bo_2);
  and and_16 (and_16_out, xor_9_out, or_3_out);
  or or_4 (S2, and_12_out, and_16_out);
  xor xor_16 (out_16, xor_15_out, and_15_out);

  // Notes on the sheet:
  //   B1+p
  //   B1p
  //   A1
  //   B1
  //   BoB1p
  //   AoBop
  //   A1+B1
  //   Ao
  //   Bo
  //   A1B1
  //   AoBo
  //   Во
  //   AoB1p
  //   Ao+Bo
  //   p
  //   AoBoB1p
  //   А1+В1
  //   Ао+Во
  //   А1В1
  //   АоВо
  //   AoB1A1p
endmodule
