// Logisim project Лаба 2.circ as structural Verilog: 1 circuit, main circuit main
module main (
  input  X1,
  input  X1_2,
  input  X2,
  input  X2_2,
  input  X3,
  input  X3_2,
  input  X1_3,
  input  X1_4,
  input  X2_3,
  input  X2_4,
  input  X3_3,
  input  X3_4,
  input  X1_5,
  input  X1_6,
  input  X2_5,
  input  X2_6,
  input  X3_5,
  input  X3_6,
  output F1,
  output F1_2,
  output F2,
  output F2_2,
  output F3,
  output F3_2
);

  wire and_1_out, and_2_out, and_3_out, and_4_out, and_5_out, and_6_out, and_7_out, nand_1_out, nand_2_out,
       nand_3_out, nand_4_out, nand_5_out, nand_6_out, nand_7_out, nand_8_out, nand_9_out, nand_10_out,
       nand_11_out, nand_12_out, nand_13_out, nand_14_out, nand_15_out, nand_16_out, not_1_out, not_2_out,
       not_3_out, not_4_out, not_5_out, not_6_out, xor_1_out;

  not not_1 (not_1_out, X1_3);
  not not_2 (not_2_out, X2_3);
  not not_3 (not_3_out, X3_3);
  not not_4 (not_4_out, X1_5);
  not not_5 (not_5_out, X2_5);
  not not_6 (not_6_out, X1);
  xor xor_1 (xor_1_out, X2, X3);
  and and_1 (and_1_out, not_1_out, X3_3, X2_3);
  and and_2 (and_2_out, not_2_out, not_3_out);
  and and_3 (and_3_out, not_4_out, not_5_out);
  and and_4 (and_4_out, X1_5, X2_5);
  and and_5 (and_5_out, not_4_out, X3_5);
  and and_6 (and_6_out, not_6_out, xor_1_out);
  and and_7 (and_7_out, X1, X3);
  or or_1 (F2, and_1_out, and_2_out);
  or or_2 (F1, and_6_out, and_7_out);
  or or_3 (F3, and_3_out, and_4_out, and_5_out);
  nand nand_1 (nand_1_out, X1_6, X1_6);
  nand nand_2 (nand_2_out, X2_6, X2_6);
  nand nand_3 (nand_3_out, X1_2, X1_2);
  nand nand_4 (nand_4_out, X2_2, X2_2);
  nand nand_5 (nand_5_out, X3_2, X3_2);
  nand nand_6 (nand_6_out, X1_4, X1_4);
  nand nand_7 (nand_7_out, X2_4, X2_4);
  nand nand_8 (nand_8_out, X3_4, X3_4);
  nand nand_9 (nand_9_out, nand_1_out, nand_2_out);
  nand nand_10 (nand_10_out, nand_1_out, X2_6, X3_6);
  nand nand_11 (nand_11_out, nand_3_out, X2_2, nand_5_out);
  nand nand_12 (nand_12_out, nand_3_out, nand_4_out, X3_2);
  nand nand_13 (nand_13_out, X3_2, X1_2);
  nand nand_14 (nand_14_out, nand_6_out, X2_4, X3_4);
  nand nand_15 (nand_15_out, nand_7_out, nand_8_out);
  nand nand_16 (nand_16_out, X1_6, X2_6);
  nand nand_17 (F1_2, nand_11_out, nand_12_out, nand_13_out);
  nand nand_18 (F2_2, nand_14_out, nand_15_out);
  nand nand_19 (F3_2, nand_9_out, nand_10_out, nand_16_out);

  // Notes on the sheet:
  //   В основном базисе
  //   В основном базисе
  //   В основном базисе
  //   В базисе Шеффера
  //   В базисе Шеффера
  //   В базисе Шеффера
endmodule
