// Logisim project lab3.circ as structural Verilog: 1 circuit, main circuit main
module main (
  input  V1,
  input  D1,
  input  D2,
  input  D3,
  input  D4,
  input  V2,
  input  C2,
  input  C1,
  output Q1,
  output Q2,
  output Q3,
  output Q4
);

  wire and_1_out, and_2_out, and_3_out, and_4_out, and_5_out, and_6_out, and_7_out, and_8_out, and_9_out,
       and_10_out, nor_1_out, nor_2_out, nor_3_out, nor_4_out, nor_5_out, not_1_out, not_2_out, not_3_out,
       not_4_out, not_5_out, not_6_out;

  not not_1 (not_1_out, V2);
  not not_2 (not_2_out, not_1_out);
  and and_1 (and_1_out, V1, not_1_out);
  and and_2 (and_2_out, D1, not_2_out);
  and and_3 (and_3_out, Q1, not_1_out);
  and and_4 (and_4_out, D2, not_2_out);
  and and_5 (and_5_out, Q2, not_1_out);
  and and_6 (and_6_out, D3, not_2_out);
  and and_7 (and_7_out, Q3, not_1_out);
  and and_8 (and_8_out, D4, not_2_out);
  nor nor_1 (nor_1_out, and_1_out, and_2_out);
  nor nor_2 (nor_2_out, and_3_out, and_4_out);
  nor nor_3 (nor_3_out, and_5_out, and_6_out);
  nor nor_4 (nor_4_out, and_7_out, and_8_out);
  and and_9 (and_9_out, V2, C2);
  and and_10 (and_10_out, not_1_out, C1);
  not not_3 (not_3_out, nor_1_out);
  not not_4 (not_4_out, nor_2_out);
  not not_5 (not_5_out, nor_3_out);
  not not_6 (not_6_out, nor_4_out);
  nor nor_5 (nor_5_out, and_9_out, and_10_out);
  J_K_Flip_Flop j_k_ff_1 (.J(not_3_out), .clk(nor_5_out), .K(nor_1_out), .Q(Q1));  // open: Qn, preset, en, reset
  J_K_Flip_Flop j_k_ff_2 (.J(not_4_out), .clk(nor_5_out), .K(nor_2_out), .Q(Q2));  // open: Qn, preset, en, reset
  J_K_Flip_Flop j_k_ff_3 (.J(not_5_out), .clk(nor_5_out), .K(nor_3_out), .Q(Q3));  // open: Qn, preset, en, reset
  J_K_Flip_Flop j_k_ff_4 (.J(not_6_out), .clk(nor_5_out), .K(nor_4_out), .Q(Q4));  // open: Qn, preset, en, reset
endmodule
